# Fritzing sketch schematic (saved by Fritzing 0.9.3b)
breadboards: 1

parts:
  Part1 = Adafruit Metro Mini [part_number="Adafruit #2590"]
  J1 = Piezo Speaker  # not connected
  R3 = Trimmer Potentiometer [maximum_resistance=10kΩ package=THT]
  Part2 = Adafruit MPR121
  Part3 = Adafruit Analog 2-Axis Joystick [part_number="Adafruit #512"]

nets:
  N1: Part1.AD5/SCL, Part2.SDA
  N2: Part1.AD4/SDA, Part2.SCL
  N3: Part1.AD2, Part3.YOUT
  N4: Part1.IO9, R3.leg1
  N5: Part1.IO2, Part2.IRQ
  +5V: Part1.+5V, Part2.VIN, Part3.VCC
  GND: Part1.GND, R3.leg2, Part2.GND, Part3.GND

custom parts:
  Adafruit Metro Mini: We sure love the ATmega328 here at Adafruit, and we use them a lot for our own projects. The processor has plenty of GPIO, Analog inputs, hardware UART SPI and I2C, timers and PWM galore - just enough for most simple projects. When we need to go small, we use a Pro Trinket 3V or 5V, but if you want to have USB-to-Serial built in, we reach for an Adafruit METRO Mini. METRO Mini is the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
  Adafruit MPR121: Add lots of touch sensors to your next microcontroller project with this easy-to-use 12-channel capacitive touch sensor breakout board, starring the MPR121. This chip can handle up to 12 individual touch pads. The MPR121 has support for only I2C, which can be implemented with nearly any microcontroller. You can select one of 4 addresses with the ADDR pin, for a total of 48 capacitive touch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
  Adafruit Analog 2-Axis Joystick: This mini-kit makes it easy to mount a PSP/Xbox-like thumb joystick to your project. The thumbstick is an analog joystick - more accurate and sensitive than just 'directional' joysticks - with a 'press in to select' button. Since it's analog, you'll need two analog reading pins on your microcontroller to determine X and Y. Having an extra digital input will let you read the switch. The pack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
